// Digital circuit 00_fsm1.dig as structural Verilog
module _00_fsm1 (
  output [31:0] IR
);

  wire Clock_out, Reset_out;
  wire [31:0] u_Marvin_CPU_mem_addr, u_Marvin_ROM_rdata;

  Button Clock (.out(Clock_out));
  Button #(.activeLow("true")) Reset (.out(Reset_out));
  Marvin_CPU #(.applicationType("IVERILOG"), .CodeFile("C:\\Users\\andre\\Downloads\\PROJECTS\\marvin_cpu\\rtl\\marvin_cpu.v")) u_Marvin_CPU (
    .clk(Clock_out), .rst_n(Reset_out), .mem_rdata(u_Marvin_ROM_rdata), .mem_addr(u_Marvin_CPU_mem_addr),
    .dbg_IR(IR));
  Marvin_ROM #(.applicationType("IVERILOG"), .CodeFile("C:\\Users\\andre\\Downloads\\PROJECTS\\marvin_cpu\\rtl\\marvin_rom.v")) u_Marvin_ROM (
    .clk(Clock_out), .addr(u_Marvin_CPU_mem_addr), .rdata(u_Marvin_ROM_rdata));
endmodule
