// Digital circuit 00_fsm2.dig as structural Verilog
module _00_fsm2 (
  output [31:0] IR
);

  wire Clock_out, Reset_out, u_Marvin_CPU_mem_valid, u_Marvin_ROM_ready;
  wire [31:0] u_Marvin_CPU_mem_addr, u_Marvin_ROM_rdata;

  Button Clock (.out(Clock_out));
  Button #(.activeLow("true")) Reset (.out(Reset_out));
  Marvin_CPU #(.applicationType("IVERILOG"), .CodeFile("C:\\Users\\andre\\Downloads\\PROJECTS\\marvin_cpu\\rtl\\marvin_cpu.v")) u_Marvin_CPU (
    .clk(Clock_out), .rst_n(Reset_out), .mem_rdata(u_Marvin_ROM_rdata), .mem_ready(u_Marvin_ROM_ready),
    .mem_addr(u_Marvin_CPU_mem_addr), .mem_valid(u_Marvin_CPU_mem_valid), .dbg_IR(IR));
  Marvin_ROM #(.applicationType("IVERILOG"), .CodeFile("C:\\Users\\andre\\Downloads\\PROJECTS\\marvin_cpu\\rtl\\marvin_rom.v")) u_Marvin_ROM (
    .clk(Clock_out), .rst_n(Reset_out), .addr(u_Marvin_CPU_mem_addr), .valid(u_Marvin_CPU_mem_valid),
    .rdata(u_Marvin_ROM_rdata), .ready(u_Marvin_ROM_ready));
endmodule
