// Digital circuit 00_fsm3.dig as structural Verilog
module _00_fsm3 (
  output [31:0] IR
);

  wire clock, ready, reset, u_Marvin_CPU_mem_valid;
  wire [31:0] rdata, u_Marvin_CPU_mem_addr;

  Button u_Clock (.out(clock));
  Button #(.activeLow("true")) u_Reset (.out(reset));
  Marvin_CPU #(.applicationType("IVERILOG"), .CodeFile("C:\\Users\\andre\\Downloads\\PROJECTS\\marvin_cpu\\rtl\\marvin_cpu.v")) u_Marvin_CPU (
    .clk(clock), .rst_n(reset), .mem_rdata(rdata), .mem_ready(ready), .mem_addr(u_Marvin_CPU_mem_addr),
    .mem_valid(u_Marvin_CPU_mem_valid), .dbg_IR(IR));
  Marvin_ROM #(.applicationType("IVERILOG"), .CodeFile("C:\\Users\\andre\\Downloads\\PROJECTS\\marvin_cpu\\rtl\\marvin_rom.v")) u_Marvin_ROM (
    .clk(clock), .rst_n(reset), .addr(u_Marvin_CPU_mem_addr), .valid(u_Marvin_CPU_mem_valid), .rdata(rdata),
    .ready(ready));
endmodule
